# Fritzing sketch gpstag (saved by Fritzing 0.9.3b)
breadboards: 1

parts:
  R1 = Resistor [tolerance=±5% resistance=100k package=THT]
  R2 = Resistor [tolerance=±5% resistance=100k package=THT]
  Grove1 = Grove OLED 128x96
  Part2 = Barometric Pressure Sensor - BMP180 Breakout (GY-68)
  U3 = LIPO-2000mAh [package=lipo-2000]
  Part3 = Arduino Pro Mini (3.3V)
  U4 = SUP500F [package=sup500f]
  S1 = Pushbutton [package="[THT]"]
  LED1 = LED - 5mm [color="Blue (525nm)" package="5 mm [THT]"]
  R3 = Resistor [tolerance=±5% resistance=220 package=THT]
  R4 = Resistor [tolerance=±5% resistance=220 package=THT]

nets:
  N1: R1.Pin_0, R2.Pin_1, Part3.A0
  GND: R1.Pin_1, Grove1.GND, Part2.GND, U3.-, Part3.GND, U4.GND, R4.Pin_0
  VCC: R2.Pin_0, Grove1.VCC, Part2.VCC, U3.+, Part3.RAW, U4.VCC, R3.Pin_0
  N2: Grove1.SDA, Part2.SDA, Part3.A4
  N3: Grove1.SCL, Part2.SCL, Part3.A5
  N4: Part3.VCC, Part3.D2, S1.Pin_1, S1.Pin_2
  N5: Part3.D6, LED1.anode
  N6: Part3.D4, U4.RX-I
  N7: Part3.D3, U4.TX-O
  N8: S1.Pin_3, S1.Pin_4, R4.Pin_1
  N9: LED1.cathode, R3.Pin_1
